# Fritzing sketch GiantButton (saved by Fritzing 0.9.3b)
breadboards: 1

parts:
  VCC1 = 4 x AAA Battery Mount
  Part1 = Photon
  R1 = Resistor [tolerance=±5% resistance=220 package=THT]
  S1 = Round Pushbutton

nets:
  N1: VCC1.-, Part1.GND, R1.Pin_0, S1.leg0
  N2: VCC1.+, Part1.VIN
  N3: Part1.WKP, R1.Pin_1, S1.leg1
